# Fritzing sketch arduino_isp_ispnub (saved by Fritzing 0.9.3b)
circuit board: 8.46667cm x 5.64444cm
breadboards: 1

parts:
  Bauteil2 = Arduino Uno (Rev3)
  U1 = ATTINY13 [package=dip]
  J1 = Piezo Speaker
  LED1 = LED - 3mm [color="Red (633nm)" package="3 mm [THT]"]
  LED2 = LED - 3mm [color="Yellow (592nm)" package="3 mm [THT]"]
  R1 = Resistor [tolerance=±5% resistance=1k package=THT]
  R2 = Resistor [tolerance=±5% resistance=1k package=THT]
  S1 = Pushbutton [package="[THT]"]
  LED3 = LED - 3mm [color="Green (565nm)" package="3 mm [THT]"]
  R3 = Resistor [tolerance=±5% resistance=1k package=THT]

nets:
  N1: Bauteil2.A0, J1.pin2
  N2: Bauteil2.A1, LED1.anode
  N3: Bauteil2.A2, LED2.anode
  N4: Bauteil2.A3, LED3.anode
  N5: Bauteil2.D10_PWM/SS, U1.PB5(NRES)
  N6: Bauteil2.D11_PWM/MOSI, U1.PB0(MOSI)
  N7: Bauteil2.D12/MISO, U1.PB1(MISO)
  N8: Bauteil2.D13/SCK, U1.PB2(SCK_ADC1)
  GND: Bauteil2.GND, U1.GND, J1.pin1, R1.Pin_1, R2.Pin_0, S1.Pin_1, S1.Pin_2, R3.Pin_1
  N9: Bauteil2.D3_PWM, S1.Pin_3, S1.Pin_4
  5V: Bauteil2.5V, U1.VCC
  N10: LED1.cathode, R1.Pin_0
  N11: LED2.cathode, R2.Pin_1
  N12: LED3.cathode, R3.Pin_0

notes:
  program via ISP
  start programming
